# Fritzing sketch robosub_v1 (saved by Fritzing 1.0.6)

parts:
  Part2 = Adafruit PCA9685 PWM/Servo Breakout [part_number=815]
  A1 = Raspberry Pi 5  # not connected
  A4 = Littlebee 40A ESC
  A8 = Littlebee 40A ESC
  A9 = Littlebee 40A ESC
  A10 = Littlebee 40A ESC
  Part3 = Adafruit BNO085 9-DOF Orientation IMU Fusion [part_number="Addfruit #4754"]
  A11 = Littlebee 40A ESC
  A12 = Littlebee 40A ESC
  A13 = Teensy 4.1
  A14 = Jetson Nano
  A15 = GY-MS5837
  J3 = Basic Servo
  J4 = Basic Servo
  U3 = TCM8240MD [package=tcm8240md]
  U4 = TCM8240MD [package=tcm8240md]
  U5 = TCM8240MD [package=tcm8240md]
  U6 = TCM8240MD [package=tcm8240md]

nets:
  GND: Part2.GND, A4.Pin_6, A8.Pin_6, A9.Pin_6, A10.Pin_6, Part3.GND, A11.Pin_6, A12.Pin_6, A13.Pin_12, A13.Pin_38, A13.Pin_50, A13.Pin_63, A15.Pin_2, J3.gnd, J4.gnd
  N1: Part2.PWM5, A12.Pin_8
  N2: Part2.5.0V, A4.Pin_7, A8.Pin_7, A9.Pin_7, A10.Pin_7, A11.Pin_7, A12.Pin_7
  N3: Part2.PWM4, A11.Pin_8
  N4: Part2.PWM3, A9.Pin_8
  N5: Part2.PWM2, A10.Pin_8
  N6: Part2.PWM1, A8.Pin_8
  N7: Part2.PWM0, A4.Pin_8
  N8: Part2.SDA, A13.Pin_28
  N9: Part2.SCL, A13.Pin_27
  N10: Part2.PWM15, J3.pulse
  N11: Part2.PWM14, J4.pulse
  N12: Part3.VCC, A13.Pin_37, A13.Pin_62
  N13: Part3.SCL/SCK/RX, A13.Pin_57
  N14: Part3.SDA/MISO/TX, A13.Pin_56
  N15: A13.Pin_54, A15.Pin_3
  N16: A13.Pin_55, A15.Pin_4
  N17: A14.GND, U3.DOUT3, U4.DOUT3, U5.DOUT3, U6.DOUT3
  N18: A14.35, U5.DOUT2
  N19: A14.37, U6.DOUT2
  N20: A14.38, U4.DOUT2
  N21: A14.40, U3.DOUT2

custom parts:
  Adafruit PCA9685 PWM/Servo Breakout: Using only two pins, control 16 free-running PWM outputs! I2C-controlled PWM driver with a built in clock. Unlike the TLC5940 family, you do not need to continuously send it signal tying up your microcontroller, its completely free running! 5V compliant, which means you can control it from a 3.3V microcontroller and still safely drive up to 6V outputs (this is good for when you want to control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
  Raspberry Pi 5: The RPi5, a faster version of the awesome Raspberry Pi4B ARM Board with 40 pin gpio.
  Littlebee 40A ESC: LittleBee 40A 2-4 LiPo Battery ESC Brushless Speed Controller for RC FPV Multicopter.
  Teensy 4.1: The Teensy is a complete USB-based microcontoller development system, in a very small footprint, capable of implementing many types of projects. All programming is done via the USB port. No special programmer is needed, only a standard micro-USB cable and a PC or Macintosh with a USB port.
  GY-MS5837: GY-MS5837 02BA 30BA Pressure Sensor Module (30BA).
